# Fritzing sketch Bluetooth - Copy (saved by Fritzing 0.9.2b)
breadboards: 1

parts:
  U1 = atmega328 [package=dip]
  C1 = Electrolytic Capacitor [capacitance=10μF package="0605 [SMD, electrolytic]"]
  C2 = Ceramic Capacitor [capacitance=100nF package="200 mil [THT, multilayer]"]
  C3 = Ceramic Capacitor [capacitance=100nF package="100 mil [THT, multilayer]"]
  XTAL1 = Crystal [frequency="16 Mhz" package=SMD]
  R1 = Resistor [tolerance=±5% resistance=1.2k package="0805 [SMD]"]
  R2 = Resistor [tolerance=±5% resistance=1.8k package="0603 [SMD]"]
  Part1 = Bluetooth HC-06

nets:
  N1: U1.RESET, U1.GND#7, C3.0, R1.Pin_1
  N2: U1.D1_(TX), C1.+
  N3: U1.XLAT1, C3.1
  N4: U1.XLAT2, C2.0, C2.1, R2.Pin_0, Part1.GND
  N5: U1.D5_(PWM), XTAL1.pin_0
  N6: U1.D6_(PWM), XTAL1.pin_1
  N7: U1.D11_(PWM), Part1.TXD
  N8: U1.A5, R1.Pin_0, R2.Pin_1, Part1.RXD
